// Logisim project cpu.circ as structural Verilog: 9 circuits, main circuit main
module main (
  input  [15:0] Teclado,
  output [15:0] Output_OP8
);

  wire button_1_out, button_2_out, button_3_out, clock, clock_1_out, counter_1_q, counter_2_q, counter_3_q,
       counter_4_q, FDX_state_0, FDX_state_1, not_1_out, not_2_out, not_3_out, not_4_out, not_5_out,
       not_6_out, OP, print_RAM, select_RAM_address, select_write_AC, select_write_RAM, stop, write_AC,
       write_IR, write_PC, write_RAM;
  wire [7:0] AC, bitselector_1_out, bitselector_2_out, bitselector_3_out, multiplexer_1_out,
       multiplexer_2_out, PC, R_ULA, UC_output;
  wire [15:0] bit_extender_1_out, IR_q, multiplexer_3_out, RAM;

  Clock clock_1 (.out(clock_1_out));
  and and_1 (clock, clock_1_out, not_1_out);
  not not_1 (not_1_out, stop);
  Counter #(.width(1), .max('h1)) counter_1 (.Q(counter_1_q), .clk(not_2_out));  // open: load, D, count, carry, clr
  not not_2 (not_2_out, clock);
  Counter #(.width(1), .max('h1)) counter_2 (.Q(counter_2_q), .clk(clock));  // open: load, D, count, carry, clr
  Counter #(.width(1), .max('h1)) counter_3 (.Q(counter_3_q), .clk(not_3_out));  // open: load, D, count, carry, clr
  not not_3 (not_3_out, clock);
  BitSelector #(.width(16), .group(8)) bitselector_1 (.in(RAM), .out(bitselector_1_out), .sel(1'b0));
  Register #(.width(16)) IR (.D(RAM), .Q(IR_q), .clk(FDX_state_0), .clr(button_1_out));  // open: en
  Button button_1 (.out(button_1_out));
  not not_4 (not_4_out, counter_2_q);
  not not_5 (not_5_out, counter_3_q);
  Multiplexer #(.width(8)) multiplexer_1 (
    .in0(bitselector_1_out), .in1(R_ULA), .out(multiplexer_1_out), .sel(select_write_AC));  // open: en
  UC uc_1 (
    .IR(IR_q), .enabled(counter_4_q), .select_RAM_address(select_RAM_address), .write_AC(write_AC),
    .\output (UC_output), .write_RAM(write_RAM), .subtract(OP), .select_write_AC(select_write_AC),
    .select_write_RAM(select_write_RAM), .print_RAM(print_RAM), .stop(stop), .write_PC(write_IR),
    .write_IR(write_PC));
  Counter #(.width(1), .max('h1), .trigger("falling")) counter_4 (
    .Q(counter_4_q), .clk(clock));  // open: load, D, count, carry, clr
  and and_2 (FDX_state_1, not_4_out, counter_1_q);
  and and_3 (FDX_state_0, counter_2_q, not_5_out);
  Register u_AC (.D(multiplexer_1_out), .en(write_AC), .Q(AC), .clk(FDX_state_1), .clr(button_2_out));
  Button button_2 (.out(button_2_out));
  assign bit_extender_1_out = {{8{1'b0}}, AC};  // Bit_Extender bit_extender_1
  BitSelector #(.width(16), .group(8)) bitselector_2 (.in(RAM), .out(bitselector_2_out), .sel(1'b0));
  Multiplexer #(.width(8)) multiplexer_2 (
    .in0(PC), .in1(UC_output), .out(multiplexer_2_out), .sel(select_RAM_address));  // open: en
  Multiplexer #(.width(16)) multiplexer_3 (
    .in0(bit_extender_1_out), .in1(Teclado), .out(multiplexer_3_out), .sel(select_write_RAM));  // open: en
  Multiplexer #(.width(16), .enable("false")) multiplexer_4 (
    .in1(RAM), .out(Output_OP8), .sel(print_RAM));  // open: in0
  Counter #(.trigger("falling")) u_PC (
    .load(write_PC), .D(bitselector_2_out), .count(not_6_out), .Q(PC), .clk(FDX_state_0), .clr(button_3_out));  // open: carry
  not not_6 (not_6_out, write_PC);
  Button button_3 (.out(button_3_out));
  ula ula_1 (.A(AC), .B(bitselector_3_out), .OP(OP), .R(R_ULA));  // open: out_4, out_5, out_6, Overflow
  BitSelector #(.width(16), .group(8)) bitselector_3 (.in(RAM), .out(bitselector_3_out), .sel(1'b0));
  RAM #(.dataWidth(16), .bus("separate")) ram_1 (
    .addr(multiplexer_2_out), .din(multiplexer_3_out), .data(RAM), .str(write_RAM), .clk(FDX_state_1));  // open: sel, ld, clr

  // Notes on the sheet:
  //   de gate delay
  //   foram utilizados múltiplos
  //   counters para resolver problemas
  //   a UC irá ser ativada e desativada a cada falling edge do clock
  //   para evitar problemas de delay
endmodule

module UC (
  input  [15:0] IR,
  input  enabled,
  output select_RAM_address,
  output write_AC,
  output write_RAM,
  output select_write_AC,
  output subtract,
  output select_write_RAM,
  output [7:0] \output ,
  output print_RAM,
  output stop,
  output write_IR,
  output write_PC
);

  wire decoder_1_out0, decoder_1_out1, decoder_1_out2, decoder_1_out3, decoder_1_out4, decoder_1_out5,
       decoder_1_out6, decoder_1_out7, decoder_1_out8, decoder_1_out9, decoder_1_out10, decoder_1_out11,
       decoder_1_out12, decoder_1_out13, decoder_1_out14, decoder_1_out15, select_RAM_address_1,
       select_RAM_address_2, select_RAM_address_3, select_RAM_address_4, select_RAM_address_7,
       select_RAM_address_8, select_write_AC_1, select_write_AC_2, write_AC_1, write_AC_2, write_AC_3,
       write_RAM_1, write_RAM_2;

  Decoder #(.select(4), .disabled(0)) decoder_1 (
    .out0(decoder_1_out0), .out1(decoder_1_out1), .out2(decoder_1_out2), .out3(decoder_1_out3),
    .out4(decoder_1_out4), .out5(decoder_1_out5), .out6(decoder_1_out6), .out7(decoder_1_out7),
    .out8(decoder_1_out8), .out9(decoder_1_out9), .out10(decoder_1_out10), .out11(decoder_1_out11),
    .out12(decoder_1_out12), .out13(decoder_1_out13), .out14(decoder_1_out14), .out15(decoder_1_out15),
    .sel(IR[11:8]), .en(enabled));
  op1 op1_1 (.enable(decoder_1_out1), .select_RAM_address(select_RAM_address_1), .write_AC(write_AC_1));
  op2 op2_1 (.enable(decoder_1_out2), .select_RAM_address(select_RAM_address_2), .write_RAM(write_RAM_1));
  op3 op3_1 (
    .enable(decoder_1_out3), .select_RAM_address(select_RAM_address_3), .write_AC(write_AC_2),
    .select_write_AC(select_write_AC_1));
  op4 op4_1 (
    .enable(decoder_1_out4), .select_RAM_address(select_RAM_address_4), .write_AC(write_AC_3),
    .select_write_AC(select_write_AC_2), .subtract(subtract));
  op7 op7_1 (
    .enable(decoder_1_out7), .select_RAM_address(select_RAM_address_7), .write_RAM(write_RAM_2),
    .select_write_RAM(select_write_RAM));
  op8 op8_1 (.enable(decoder_1_out8), .select_RAM_address(select_RAM_address_8), .print_RAM(print_RAM));
  op9 op9_1 (.enable(decoder_1_out9), .stop(write_IR), .write_PC(write_PC), .write_IR(stop));
  or or_1 (write_AC, write_AC_1, write_AC_2, write_AC_3);
  or or_2 (write_RAM, write_RAM_1, write_RAM_2);
  or or_3 (select_write_AC, select_write_AC_1, select_write_AC_2);
  or or_4 (select_RAM_address, select_RAM_address_1, select_RAM_address_2, select_RAM_address_3, select_RAM_address_4, select_RAM_address_7, select_RAM_address_8);

  assign \output  = IR[7:0];

  // Other names for the same wires on the sheet: instruction[3:0] = IR[11:8]; complement[7:0] = IR[7:0]
endmodule

module op1 (
  input  enable,
  output select_RAM_address,
  output write_AC
);


  assign select_RAM_address = enable;
  assign write_AC = enable;
endmodule

module op2 (
  input  enable,
  output select_RAM_address,
  output write_RAM
);


  assign select_RAM_address = enable;
  assign write_RAM = enable;
endmodule

module op3 (
  input  enable,
  output select_RAM_address,
  output write_AC,
  output select_write_AC
);


  assign select_RAM_address = enable;
  assign select_write_AC = enable;
  assign write_AC = enable;
endmodule

module op4 (
  input  enable,
  output select_RAM_address,
  output write_AC,
  output select_write_AC,
  output subtract
);


  assign select_RAM_address = enable;
  assign select_write_AC = enable;
  assign subtract = enable;
  assign write_AC = enable;
endmodule

module op7 (
  input  enable,
  output select_RAM_address,
  output write_RAM,
  output select_write_RAM
);


  assign select_RAM_address = enable;
  assign select_write_RAM = enable;
  assign write_RAM = enable;
endmodule

module op8 (
  input  enable,
  output select_RAM_address,
  output print_RAM
);


  assign print_RAM = enable;
  assign select_RAM_address = enable;
endmodule

module op9 (
  input  enable,
  output write_IR,
  output write_PC,
  output stop
);


  assign stop = enable;
  assign write_IR = enable;
  assign write_PC = enable;
endmodule
